// Logisim project atividade-de-aula.circ as structural Verilog: 1 circuit, main circuit main
module main (
  input  A_0,
  input  A,
  input  A_3,
  input  B_0,
  input  B,
  input  A_1,
  input  A_4,
  input  B_1,
  input  B_3,
  input  A_5,
  input  A_2,
  input  A_6,
  input  B_4,
  input  B_2,
  input  A_7,
  input  B_5
);

  wire and_1_out, and_2_out, and_3_out, and_4_out, not_1_out, or_1_out, xnor_1_out, xnor_2_out, xnor_3_out,
       xnor_4_out, xor_1_out;

  LED S (.in(not_1_out));
  not not_1 (not_1_out, A);
  and and_1 (and_1_out, A_4, B_3);
  and and_2 (and_2_out, A_6, A_6, A_6);
  LED S_2 (.in(and_1_out));
  LED S_3 (.in(and_2_out));
  xor xor_1 (xor_1_out, A_7, B_5);
  LED S_4 (.in(xor_1_out));
  or or_1 (or_1_out, A_3, B);
  xnor xnor_1 (xnor_1_out, A_5, B_4);
  LED S_5 (.in(or_1_out));
  LED led_1 (.in(xnor_1_out));
  xnor xnor_2 (xnor_2_out, A_0, B_0);
  xnor xnor_3 (xnor_3_out, A_1, B_1);
  xnor xnor_4 (xnor_4_out, A_2, B_2);
  and and_3 (and_3_out, xnor_2_out, xnor_3_out);
  and and_4 (and_4_out, and_3_out, xnor_4_out);
  LED led_2 (.in(and_4_out));

  // Notes on the sheet:
  //   Porta NOT
  //   Porta AND
  //   Porta XOR
  //   Porta XOR
  //   Porta XNOR
  //   Comparador de 3 Bits
endmodule
