// Logisim project Conversor-Binario.circ as structural Verilog: 1 circuit, main circuit main
module main (
  input  in_1,
  input  in_2,
  input  in_3,
  input  in_4
);

  wire xor_1_out, xor_2_out, xor_3_out;

  LED led_1 (.in(in_1));
  LED led_2 (.in(xor_1_out));
  xor xor_1 (xor_1_out, in_1, in_2);
  LED led_3 (.in(xor_2_out));
  xor xor_2 (xor_2_out, in_2, in_3);
  xor xor_3 (xor_3_out, in_3, in_4);
  LED led_4 (.in(xor_3_out));

  // Notes on the sheet:
  //   Código Binário
  //   CBR [GRAY]
  //   S[3]
  //   S[2]
  //   S[1]
  //   S[0]
  //   Código Gray
endmodule
