// Logisim project decodificador-binario.circ as structural Verilog: 1 circuit, main circuit main
module main (
  input  A_2,
  input  A_1,
  input  A_0
);

  wire not_1_out, not_2_out, not_3_out, Z_0_out, Z_1_out, Z_2_out, Z_3_out, Z_4_out, Z_5_out, Z_6_out,
       Z_7_out;

  not not_1 (not_1_out, A_2);
  not not_2 (not_2_out, A_1);
  not not_3 (not_3_out, A_0);
  LED led_1 (.in(Z_0_out));
  and Z_0 (Z_0_out, not_1_out, not_2_out, not_3_out);
  and Z_1 (Z_1_out, not_1_out, not_2_out, A_0);
  LED led_2 (.in(Z_1_out));
  LED led_3 (.in(Z_2_out));
  and Z_2 (Z_2_out, not_1_out, A_1, not_3_out);
  LED led_4 (.in(Z_3_out));
  and Z_3 (Z_3_out, not_1_out, A_1, A_0);
  LED led_5 (.in(Z_4_out));
  and Z_4 (Z_4_out, A_2, not_2_out, not_3_out);
  and Z_5 (Z_5_out, A_2, not_2_out, A_0);
  LED led_6 (.in(Z_5_out));
  and Z_6 (Z_6_out, A_2, A_1, not_3_out);
  LED led_7 (.in(Z_6_out));
  and Z_7 (Z_7_out, A_2, A_1, A_0);
  LED led_8 (.in(Z_7_out));

  // Notes on the sheet:
  //   Decodificador Binário
endmodule
