// Logisim project detector-paridade-impar.circ as structural Verilog: 1 circuit, main circuit main
module main (
  input  S1,
  input  S2,
  input  A,
  input  B,
  input  C,
  input  D,
  input  S3,
  input  in_8,
  input  in_9,
  input  [2:0] in_10,
  output S,
  output S_2,
  output out_13
);

  wire and_1_out, and_2_out, and_3_out, and_4_out, not_1_out, not_2_out, not_3_out;

  xor odd_parity_1 (S, S1, S2, S3);
  Multiplexer #(.select(3), .enable("false")) multiplexer_1 (
    .in0(in_9), .in1(in_8), .in2(in_8), .in3(in_9), .in4(in_8), .in5(in_9), .in6(in_9), .in7(in_8),
    .out(out_13), .sel(in_10));
  not not_1 (not_1_out, A);
  not not_2 (not_2_out, B);
  not not_3 (not_3_out, C);
  and and_1 (and_1_out, not_1_out, not_2_out, C, D);
  and and_2 (and_2_out, not_1_out, B, not_3_out, D);
  and and_3 (and_3_out, A, not_2_out, not_3_out, D);
  and and_4 (and_4_out, A, B, C, D);
  or or_1 (S_2, and_1_out, and_2_out, and_3_out, and_4_out);

  // Notes on the sheet:
  //   Detector de Paridade Ímpar
endmodule
