// Logisim project aplicando-demux.circ as structural Verilog: 1 circuit, main circuit main
module main (
  input  D,
  input  D_2,
  input  in_3,
  input  C,
  input  in_5,
  input  D_3,
  input  H,
  input  [1:0] C_2,
  input  C0,
  input  C1,
  output S0,
  output S0_2,
  output S1,
  output S1_2,
  output out_15,
  output out_16,
  output out_17,
  output out_18,
  output out_19,
  output out_20,
  output out_21,
  output out_22
);

  wire demultiplexer_3_out0, demultiplexer_3_out1, not_1_out;

  Demultiplexer #(.select(2)) demultiplexer_1 (
    .out0(out_15), .out1(out_17), .out2(out_19), .out3(out_20), .in(in_5), .sel(C_2), .en(H));
  Demultiplexer #(.enable("false")) demultiplexer_2 (.out0(S0), .out1(S1), .in(D), .sel(in_3));
  Demultiplexer #(.enable("false")) demultiplexer_3 (
    .out0(demultiplexer_3_out0), .out1(demultiplexer_3_out1), .in(D_3), .sel(C0));
  and and_1 (S0_2, D_2, not_1_out);
  not not_1 (not_1_out, C);
  and and_2 (S1_2, C, D_2);
  Demultiplexer #(.enable("false")) demultiplexer_4 (.out0(out_16), .out1(out_18), .in(demultiplexer_3_out0), .sel(C1));
  Demultiplexer #(.enable("false")) demultiplexer_5 (.out0(out_21), .out1(out_22), .in(demultiplexer_3_out1), .sel(C1));

  // Notes on the sheet:
  //   Demux 1:2
  //   Demux 1:4
endmodule
