// Logisim project aplicando-mux.circ as structural Verilog: 1 circuit, main circuit main
module main (
  input  X0,
  input  X0_2,
  input  X1,
  input  X1_2,
  input  C,
  input  H,
  input  C_2,
  input  H_2,
  input  X0_3,
  input  X1_3,
  input  X2,
  input  X3,
  input  C0,
  input  H_3,
  input  C1,
  output S,
  output S_2,
  output S_3
);

  wire and_1_out, and_2_out, multiplexer_2_out, multiplexer_3_out, not_1_out;

  Multiplexer multiplexer_1 (.in0(X0_2), .in1(X1_2), .out(S), .sel(C), .en(H));
  Multiplexer multiplexer_2 (.in0(X0_3), .in1(X1_3), .out(multiplexer_2_out), .sel(C0), .en(H_3));
  Multiplexer multiplexer_3 (.in0(X2), .in1(X3), .out(multiplexer_3_out), .sel(C0), .en(H_3));
  Multiplexer multiplexer_4 (.in0(multiplexer_2_out), .in1(multiplexer_3_out), .out(S_3), .sel(C1), .en(H_3));
  not not_1 (not_1_out, C_2);
  and and_1 (and_1_out, X0, not_1_out, H_2);
  and and_2 (and_2_out, X1, C_2, H_2);
  or or_1 (S_2, and_1_out, and_2_out);

  // Notes on the sheet:
  //   MUX 2:1
  //   MUX 4:1
endmodule
