// Logisim project meio-subtrator.circ as structural Verilog: 1 circuit, main circuit main
module main (
  input  A,
  input  B,
  output S,
  output Ts
);

  xor xor_1 (S, A, B);
  and and_1 (Ts, ~A, B);  // AND_Gate

  // Notes on the sheet:
  //   Meio Subtrator
endmodule
