// Logisim project subtrator-completo.circ as structural Verilog: 1 circuit, main circuit main
module main (
  input  A,
  input  B,
  input  Te,
  output S,
  output Ts
);

  wire and_1_out, and_2_out, and_3_out, xor_1_out;

  xor xor_1 (xor_1_out, A, B);
  and and_1 (and_1_out, ~A, B);  // AND_Gate
  and and_2 (and_2_out, ~A, Te);  // AND_Gate
  and and_3 (and_3_out, B, Te);
  xor xor_2 (S, xor_1_out, Te);
  or or_1 (Ts, and_1_out, and_2_out, and_3_out);

  // Notes on the sheet:
  //   Subtrator Completo
endmodule
