// Logisim project igualdade-c1.circ as structural Verilog: 1 circuit, main circuit main
module main (
  input  M,
  input  A,
  output out_3
);

  xor xor_1 (out_3, M, A);

  // Notes on the sheet:
  //   Igualdade e Complemento de 1
endmodule
