// Logisim project meio-somador.circ as structural Verilog: 1 circuit, main circuit main
module main (
  input  A,
  input  B
);

  wire and_1_out, xor_1_out;

  xor xor_1 (xor_1_out, A, B);
  and and_1 (and_1_out, B, A);
  LED S (.in(xor_1_out));
  LED Ts (.in(and_1_out));

  // Notes on the sheet:
  //   Meio Somador
endmodule
