// Logisim project somador-completo.circ as structural Verilog: 1 circuit, main circuit main
module main (
  input  A,
  input  B,
  input  Te
);

  wire and_1_out, and_2_out, and_3_out, or_1_out, xor_1_out, xor_2_out;

  xor xor_1 (xor_1_out, A, B);
  and and_1 (and_1_out, A, B);
  and and_2 (and_2_out, A, Te);
  and and_3 (and_3_out, Te, B);
  xor xor_2 (xor_2_out, xor_1_out, Te);
  or or_1 (or_1_out, and_1_out, and_2_out, and_3_out);
  LED S (.in(xor_2_out));
  LED Ts (.in(or_1_out));

  // Notes on the sheet:
  //   Somador Completo
endmodule
