// Logisim project exp01_at02.circ as structural Verilog: 1 circuit, main circuit main
module main (
  input  X2,
  input  X1,
  input  X0
);

  wire and_1_out;

  and and_1 (and_1_out, X2, X1, X0);
  LED led_1 (.in(and_1_out));

  // Notes on the sheet:
  //   Porta AND com três entradas
  //   X
endmodule
