// Logisim project exp02_at02.circ as structural Verilog: 1 circuit, main circuit main
module main (
  input  A,
  input  B
);

  wire nand_1_out, nand_2_out, nand_3_out, not_1_out, not_2_out, not_3_out;

  not not_1 (not_1_out, A);
  nand nand_1 (nand_1_out, not_1_out, B);
  not not_2 (not_2_out, B);
  nand nand_2 (nand_2_out, A, not_2_out);
  nand nand_3 (nand_3_out, nand_2_out, nand_1_out);
  not not_3 (not_3_out, nand_3_out);
  LED led_1 (.in(not_3_out));

  // Notes on the sheet:
  //   XNOR com NAND e inversores 
  //   X
  //   Y
  //   W
  //   Z
endmodule
