// Logisim project exp03_at02.circ as structural Verilog: 1 circuit, main circuit main
module main (
  input  A_0,
  input  B_0,
  input  A_1,
  input  B_1,
  input  A_2,
  input  B_2
);

  wire and_1_out, nand_1_out, nand_2_out, nand_3_out, nand_4_out, nand_5_out, nand_6_out, nand_7_out,
       nand_8_out, nand_9_out, not_1_out, not_2_out, not_3_out, not_4_out, not_5_out, not_6_out, not_7_out,
       not_8_out, not_9_out;

  not not_1 (not_1_out, A_0);
  not not_2 (not_2_out, B_0);
  not not_3 (not_3_out, A_1);
  not not_4 (not_4_out, B_1);
  not not_5 (not_5_out, A_2);
  not not_6 (not_6_out, B_2);
  nand nand_1 (nand_1_out, not_1_out, B_0);
  nand nand_2 (nand_2_out, not_3_out, B_1);
  nand nand_3 (nand_3_out, not_5_out, B_2);
  nand nand_4 (nand_4_out, A_0, not_2_out);
  nand nand_5 (nand_5_out, A_1, not_4_out);
  nand nand_6 (nand_6_out, A_2, not_6_out);
  nand nand_7 (nand_7_out, nand_4_out, nand_1_out);
  nand nand_8 (nand_8_out, nand_5_out, nand_2_out);
  nand nand_9 (nand_9_out, nand_6_out, nand_3_out);
  not not_7 (not_7_out, nand_7_out);
  not not_8 (not_8_out, nand_8_out);
  not not_9 (not_9_out, nand_9_out);
  and and_1 (and_1_out, not_7_out, not_8_out, not_9_out);
  LED led_1 (.in(and_1_out));

  // Notes on the sheet:
  //   X
  //   X
  //   X
  //   Comparador de 3 bits
  //   Y
  //   Y
  //   Y
  //   W
  //   W
  //   W
endmodule
