// Logisim project Conversor_de_Codigo.circ as structural Verilog: 1 circuit, main circuit main
module main (
  input  X_2,
  input  X_1,
  input  X_0
);

  wire and_1_out, and_2_out, and_3_out, and_4_out, not_1_out, not_2_out, not_3_out, or_1_out, or_2_out,
       xor_1_out, xor_2_out, xor_3_out;

  not not_1 (not_1_out, X_2);
  not not_2 (not_2_out, X_1);
  not not_3 (not_3_out, X_0);
  xor xor_1 (xor_1_out, X_2, X_1);
  xor xor_2 (xor_2_out, X_2, X_0);
  and and_1 (and_1_out, X_0, xor_1_out);
  and and_2 (and_2_out, X_2, not_3_out);
  and and_3 (and_3_out, X_1, not_1_out);
  and and_4 (and_4_out, not_2_out, xor_2_out);
  or or_1 (or_1_out, and_1_out, and_2_out);
  xor xor_3 (xor_3_out, X_2, X_1);
  or or_2 (or_2_out, and_3_out, and_4_out);
  LED led_1 (.in(X_2));
  LED led_2 (.in(or_1_out));
  LED led_3 (.in(xor_3_out));
  LED led_4 (.in(or_2_out));

  // Notes on the sheet:
  //   Conversor de Código
  //   Y[2]
  //   Y[1]
  //   Y[0]
  //   Y[3]
endmodule
