// Logisim project Codificador-Binario.circ as structural Verilog: 1 circuit, main circuit main
module main (
  input  X_7,
  input  X_6,
  input  X_5,
  input  X_4,
  input  X_3,
  input  X_2,
  input  X_1,
  input  X_0
);

  wire Z_0_out, Z_1_out, Z_2_out;

  or Z_2 (Z_2_out, X_4, X_5, X_6, X_7);
  or Z_1 (Z_1_out, X_2, X_3, X_6, X_7);
  or Z_0 (Z_0_out, X_1, X_3, X_5, X_7);
  LED led_1 (.in(Z_2_out));
  LED led_2 (.in(Z_1_out));
  LED led_3 (.in(Z_0_out));

  // Notes on the sheet:
  //   Codificador Binário
endmodule
