// Logisim project Decodificador-Binario.circ as structural Verilog: 1 circuit, main circuit main
module main (
  input  A_1,
  input  A_0,
  input  H
);

  wire and_1_out, and_2_out, and_3_out, and_4_out, not_1_out, not_2_out;

  not not_1 (not_1_out, A_1);
  not not_2 (not_2_out, A_0);
  LED led_1 (.in(and_1_out));
  and and_1 (and_1_out, not_1_out, not_2_out, H);
  and and_2 (and_2_out, not_1_out, A_0, H);
  LED led_2 (.in(and_2_out));
  LED led_3 (.in(and_3_out));
  and and_3 (and_3_out, A_1, not_2_out, H);
  and and_4 (and_4_out, A_1, A_0, H);
  LED led_4 (.in(and_4_out));

  // Notes on the sheet:
  //   Decodificador Binário
  //   Z[0]
  //   Z[1]
  //   Z[2]
  //   Z[3]
endmodule
