// Logisim project atividade-codificador-e-decodificador.circ as structural Verilog: 1 circuit, main circuit main
module main (
  input  Z_0,
  input  Z_1,
  input  Z_2,
  input  Z_3
);

  wire and_1_out, and_2_out, and_3_out, and_4_out, not_1_out, not_2_out, or_1_out, or_2_out, or_3_out;

  or or_1 (or_1_out, Z_3, Z_2, Z_1, Z_0);
  or or_2 (or_2_out, Z_2, Z_3);
  or or_3 (or_3_out, Z_1, Z_3);
  not not_1 (not_1_out, or_2_out);
  not not_2 (not_2_out, or_3_out);
  and and_1 (and_1_out, not_1_out, not_2_out, or_1_out);
  and and_2 (and_2_out, not_1_out, or_3_out, or_1_out);
  and and_3 (and_3_out, or_2_out, not_2_out, or_1_out);
  and and_4 (and_4_out, or_2_out, or_3_out, or_1_out);
  LED led_1 (.in(and_1_out));
  LED led_2 (.in(and_2_out));
  LED led_3 (.in(and_3_out));
  LED led_4 (.in(and_4_out));

  // Notes on the sheet:
  //   Aplicação de Criptografia de Mensagem Bit a Bit
  //   Z[0]
  //   Z[1]
  //   Z[2]
  //   Z[3]
endmodule
