// Logisim project questao-1-c.circ as structural Verilog: 1 circuit, main circuit main
module main (
  input  C,
  input  B,
  input  A,
  input  S,
  input  D0,
  input  D1,
  input  D2,
  input  D3,
  input  D4,
  input  D5,
  input  D6,
  input  D7,
  output Y,
  output W
);

  wire not_1_out, not_2_out, not_3_out, not_4_out, Y1_out, Y2_out, Y3_out, Y4_out, Y5_out, Y6_out, Y7_out,
       YO_out;

  not not_1 (not_1_out, C);
  not not_2 (not_2_out, B);
  not not_3 (not_3_out, S);
  not not_4 (not_4_out, A);
  and YO (YO_out, not_1_out, not_2_out, D0, not_4_out, not_3_out);
  and Y1 (Y1_out, not_1_out, not_2_out, D1, A, not_3_out);
  and Y2 (Y2_out, not_1_out, B, D2, not_4_out, not_3_out);
  and Y3 (Y3_out, not_1_out, B, D3, A, not_3_out);
  and Y4 (Y4_out, C, not_2_out, D4, not_4_out, not_3_out);
  and Y5 (Y5_out, C, not_2_out, D5, A, not_3_out);
  and Y6 (Y6_out, C, B, D6, not_4_out, not_3_out);
  and Y7 (Y7_out, C, B, D7, A, not_3_out);
  or or_1 (Y, YO_out, Y1_out, Y2_out, Y3_out, Y4_out, Y5_out, Y6_out, Y7_out);
  not not_5 (W, Y);
endmodule
