// Logisim project questao-1-d.circ as structural Verilog: 1 circuit, main circuit main
module main (
  input  D0,
  input  D1,
  input  D2,
  input  D3,
  input  D4,
  input  D5,
  input  D6,
  input  D7,
  input  D8,
  input  D9,
  input  D10,
  input  D11,
  input  D12,
  input  D13,
  input  D14,
  input  D15,
  input  [1:0] AB,
  input  [1:0] CD,
  output S
);

  wire multiplexer_1_out, multiplexer_2_out, multiplexer_3_out, multiplexer_4_out;

  Multiplexer #(.select(2), .enable("false")) multiplexer_1 (
    .in0(D0), .in1(D1), .in2(D2), .in3(D3), .out(multiplexer_1_out), .sel(CD));
  Multiplexer #(.select(2), .enable("false")) multiplexer_2 (
    .in0(D4), .in1(D5), .in2(D6), .in3(D7), .out(multiplexer_2_out), .sel(CD));
  Multiplexer #(.select(2), .enable("false")) multiplexer_3 (
    .in0(D8), .in1(D9), .in2(D10), .in3(D11), .out(multiplexer_3_out), .sel(CD));
  Multiplexer #(.select(2), .enable("false")) multiplexer_4 (
    .in0(D12), .in1(D13), .in2(D14), .in3(D15), .out(multiplexer_4_out), .sel(CD));
  Multiplexer #(.select(2), .enable("false")) multiplexer_5 (
    .in0(multiplexer_1_out), .in1(multiplexer_2_out), .in2(multiplexer_3_out), .in3(multiplexer_4_out),
    .out(S), .sel(AB));
endmodule
