// Logisim project questao-2-a.circ as structural Verilog: 1 circuit, main circuit main
module main (
  input  E,
  input  [2:0] S,
  output D0,
  output D1,
  output D2,
  output D3,
  output D4,
  output D5,
  output D6,
  output D7
);

  Demultiplexer #(.select(3), .enable("false")) demultiplexer_1 (
    .out0(D0), .out1(D1), .out2(D2), .out3(D3), .out4(D4), .out5(D5), .out6(D6), .out7(D7), .in(E), .sel(S));
endmodule
