// Logisim project questao-2-b.circ as structural Verilog: 1 circuit, main circuit main
module main (
  input  S2,
  input  S1,
  input  S0,
  input  E,
  output D0,
  output D1,
  output D2,
  output D3,
  output D4,
  output D5,
  output D6,
  output D7
);

  wire not_1_out, not_2_out, not_3_out;

  not not_1 (not_1_out, S2);
  not not_2 (not_2_out, S1);
  not not_3 (not_3_out, S0);
  and and_1 (D0, not_1_out, not_2_out, not_3_out, E);
  and and_2 (D1, not_1_out, not_2_out, S0, E);
  and and_3 (D2, not_1_out, S1, not_3_out, E);
  and and_4 (D3, not_1_out, S1, S0, E);
  and and_5 (D4, S2, not_2_out, not_3_out, E);
  and and_6 (D5, S2, not_2_out, S0, E);
  and and_7 (D6, S2, S1, not_3_out, E);
  and and_8 (D7, S2, S1, S0, E);
endmodule
