// Logisim project questao-3-b.circ as structural Verilog: 1 circuit, main circuit main
module main (
  input  C,
  input  B,
  input  A,
  output Y
);

  wire not_1_out, not_2_out, not_3_out, Y1_out, Y2_out, Y3_out, Y4_out, Y5_out, Y6_out, Y7_out, YO_out;

  not not_1 (not_1_out, C);
  not not_2 (not_2_out, B);
  not not_3 (not_3_out, A);
  and YO (YO_out, not_1_out, not_2_out, not_3_out, 1'b1);
  and Y1 (Y1_out, not_1_out, not_2_out, A, 1'b0);
  and Y2 (Y2_out, not_1_out, B, not_3_out, 1'b0);
  and Y3 (Y3_out, not_1_out, B, A, 1'b1);
  and Y4 (Y4_out, C, not_2_out, not_3_out, 1'b0);
  and Y5 (Y5_out, C, not_2_out, A, 1'b1);
  and Y6 (Y6_out, C, B, not_3_out, 1'b1);
  and Y7 (Y7_out, C, B, A, 1'b0);
  or or_1 (Y, YO_out, Y1_out, Y2_out, Y3_out, Y4_out, Y5_out, Y6_out, Y7_out);
endmodule
