// Logisim project registrador-4bits.circ as structural Verilog: 1 circuit, main circuit main
module main (
  input  I_3,
  input  I_2,
  input  I_1,
  input  I_0,
  input  SS_SP,
  output S_3,
  output S_2,
  output S_1,
  output S_0
);

  wire clock_1_out, multiplexer_1_out, multiplexer_2_out, multiplexer_3_out, multiplexer_4_out, not_1_out,
       not_2_out, not_3_out, not_4_out;

  Clock clock_1 (.out(clock_1_out));
  Multiplexer multiplexer_1 (.in0(1'b0), .in1(I_3), .out(multiplexer_1_out), .sel(SS_SP));  // open: en
  J_K_Flip_Flop j_k_ff_1 (
    .J(multiplexer_1_out), .clk(clock_1_out), .K(not_1_out), .Q(S_3));  // open: Qn, preset, en, reset
  not not_1 (not_1_out, multiplexer_1_out);
  Multiplexer multiplexer_2 (.in0(S_3), .in1(I_2), .out(multiplexer_2_out), .sel(SS_SP));  // open: en
  not not_2 (not_2_out, multiplexer_2_out);
  J_K_Flip_Flop j_k_ff_2 (
    .J(multiplexer_2_out), .clk(clock_1_out), .K(not_2_out), .Q(S_2));  // open: Qn, preset, en, reset
  Multiplexer multiplexer_3 (.in0(S_2), .in1(I_1), .out(multiplexer_3_out), .sel(SS_SP));  // open: en
  not not_3 (not_3_out, multiplexer_3_out);
  J_K_Flip_Flop j_k_ff_3 (
    .J(multiplexer_3_out), .clk(clock_1_out), .K(not_3_out), .Q(S_1));  // open: Qn, preset, en, reset
  not not_4 (not_4_out, multiplexer_4_out);
  Multiplexer multiplexer_4 (.in0(S_1), .in1(I_0), .out(multiplexer_4_out), .sel(SS_SP));  // open: en
  J_K_Flip_Flop j_k_ff_4 (
    .J(multiplexer_4_out), .clk(clock_1_out), .K(not_4_out), .Q(S_0));  // open: Qn, preset, en, reset

  // Notes on the sheet:
  //   CLK
endmodule
