// Logisim project alarme-residencial.circ as structural Verilog
module comparador_4bits (
  input  in_1,
  input  in_2,
  input  in_3,
  input  in_4,
  input  in_5,
  input  in_6,
  input  in_7,
  input  in_8,
  output out_9
);

  wire and_nand_1_out_3, and_nand_2_out_3, xnor_nand_1_out_3, xnor_nand_2_out_3, xnor_nand_3_out_3,
       xnor_nand_4_out_3;

  xnor_nand xnor_nand_1 (.in_1(in_1), .in_2(in_2), .out_3(xnor_nand_1_out_3));
  xnor_nand xnor_nand_2 (.in_1(in_3), .in_2(in_4), .out_3(xnor_nand_2_out_3));
  xnor_nand xnor_nand_3 (.in_1(in_5), .in_2(in_6), .out_3(xnor_nand_3_out_3));
  xnor_nand xnor_nand_4 (.in_1(in_7), .in_2(in_8), .out_3(xnor_nand_4_out_3));
  and_nand and_nand_1 (.in_1(xnor_nand_1_out_3), .in_2(xnor_nand_2_out_3), .out_3(and_nand_1_out_3));
  and_nand and_nand_2 (.in_1(xnor_nand_3_out_3), .in_2(xnor_nand_4_out_3), .out_3(and_nand_2_out_3));
  and_nand and_nand_3 (.in_1(and_nand_1_out_3), .in_2(and_nand_2_out_3), .out_3(out_9));
endmodule

module xnor_nand (
  input  in_1,
  input  in_2,
  output out_3
);

  wire nand_1_out, nand_2_out, nand_3_out, nand_4_out;

  nand nand_1 (nand_1_out, in_1, in_2);
  nand nand_2 (nand_2_out, in_1, nand_1_out);
  nand nand_3 (nand_3_out, nand_1_out, in_2);
  nand nand_4 (nand_4_out, nand_2_out, nand_3_out);
  nand nand_5 (out_3, nand_4_out, nand_4_out);
endmodule

module and_nand (
  input  in_1,
  input  in_2,
  output out_3
);

  wire nand_1_out;

  nand nand_1 (nand_1_out, in_1, in_2);
  nand nand_2 (out_3, nand_1_out, nand_1_out);
endmodule

module entrada_senha (
  input  in_1,
  input  in_2,
  input  in_3,
  input  in_4,
  input  in_5,
  input  in_6,
  input  in_7,
  input  in_8,
  input  in_9,
  input  in_10,
  input  in_11,
  input  in_12,
  input  in_13,
  input  in_14,
  input  in_15,
  input  in_16,
  input  in_17,
  input  in_18,
  input  in_19,
  input  in_20,
  input  in_21,
  input  in_22,
  input  in_23,
  input  in_24,
  input  in_25,
  input  in_26,
  input  in_27,
  input  in_28,
  input  in_29,
  input  in_30,
  input  in_31,
  input  in_32,
  input  in_33,
  input  in_34,
  input  in_35,
  input  in_36,
  input  in_37,
  input  in_38,
  input  in_39,
  input  in_40,
  input  in_41,
  input  in_42,
  input  in_43,
  input  in_44,
  input  in_45,
  input  in_46,
  input  in_47,
  input  in_48,
  input  in_49,
  input  in_50,
  input  in_51,
  input  in_52,
  input  in_53,
  input  in_54,
  input  in_55,
  input  in_56,
  input  in_57,
  input  in_58,
  input  in_59,
  input  in_60,
  input  in_61,
  input  in_62,
  input  in_63,
  input  in_64,
  input  in_65,
  input  in_66,
  input  in_67,
  input  in_68,
  input  in_69,
  input  in_70,
  input  in_71,
  input  in_72,
  input  in_73,
  input  in_74,
  input  in_75,
  input  in_76,
  input  in_77,
  input  in_78,
  input  in_79,
  input  in_80,
  input  in_81,
  input  in_82,
  input  in_83,
  input  in_84,
  input  in_85,
  input  in_86,
  input  in_87,
  input  in_88,
  input  in_89,
  input  in_90,
  input  in_91,
  input  in_92,
  input  in_93,
  input  in_94,
  input  in_95,
  input  in_96,
  input  in_97,
  input  in_98,
  input  in_99,
  input  in_100,
  input  in_101,
  input  in_102,
  input  in_103,
  input  in_104,
  input  in_105,
  input  in_106,
  input  in_107,
  input  in_108,
  input  in_109,
  input  in_110,
  input  in_111,
  input  in_112,
  input  in_113,
  input  in_114,
  input  in_115,
  input  in_116,
  input  in_117,
  input  in_118,
  input  in_119,
  input  in_120,
  output out_121
);

  wire and_nand_1_out_3, and_nand_2_out_3, and_nand_3_out_3, and_nand_4_out_3, codificador_4bits_1_out_11,
       codificador_4bits_1_out_12, codificador_4bits_1_out_13, codificador_4bits_1_out_14,
       codificador_4bits_2_out_11, codificador_4bits_2_out_12, codificador_4bits_2_out_13,
       codificador_4bits_2_out_14, codificador_4bits_3_out_11, codificador_4bits_3_out_12,
       codificador_4bits_3_out_13, codificador_4bits_3_out_14, codificador_4bits_4_out_11,
       codificador_4bits_4_out_12, codificador_4bits_4_out_13, codificador_4bits_4_out_14,
       codificador_4bits_5_out_11, codificador_4bits_5_out_12, codificador_4bits_5_out_13,
       codificador_4bits_5_out_14, codificador_4bits_6_out_11, codificador_4bits_6_out_12,
       codificador_4bits_6_out_13, codificador_4bits_6_out_14, codificador_4bits_7_out_11,
       codificador_4bits_7_out_12, codificador_4bits_7_out_13, codificador_4bits_7_out_14,
       codificador_4bits_8_out_11, codificador_4bits_8_out_12, codificador_4bits_8_out_13,
       codificador_4bits_8_out_14, codificador_4bits_9_out_11, codificador_4bits_9_out_12,
       codificador_4bits_9_out_13, codificador_4bits_9_out_14, codificador_4bits_10_out_11,
       codificador_4bits_10_out_12, codificador_4bits_10_out_13, codificador_4bits_10_out_14,
       codificador_4bits_11_out_11, codificador_4bits_11_out_12, codificador_4bits_11_out_13,
       codificador_4bits_11_out_14, codificador_4bits_12_out_11, codificador_4bits_12_out_12,
       codificador_4bits_12_out_13, codificador_4bits_12_out_14, comparador_4bits_1_out_9,
       comparador_4bits_2_out_9, comparador_4bits_3_out_9, comparador_4bits_4_out_9,
       comparador_4bits_5_out_9, comparador_4bits_6_out_9;

  codificador_4bits codificador_4bits_1 (
    .in_1(in_5), .in_2(in_11), .in_3(in_17), .in_4(in_23), .in_5(in_29), .in_6(in_35), .in_7(in_41),
    .in_8(in_47), .in_9(in_53), .in_10(in_59), .out_11(codificador_4bits_1_out_11),
    .out_12(codificador_4bits_1_out_12), .out_13(codificador_4bits_1_out_13),
    .out_14(codificador_4bits_1_out_14));
  codificador_4bits codificador_4bits_2 (
    .in_1(in_65), .in_2(in_71), .in_3(in_77), .in_4(in_83), .in_5(in_89), .in_6(in_95), .in_7(in_101),
    .in_8(in_107), .in_9(in_113), .in_10(in_119), .out_11(codificador_4bits_2_out_11),
    .out_12(codificador_4bits_2_out_12), .out_13(codificador_4bits_2_out_13),
    .out_14(codificador_4bits_2_out_14));
  comparador_4bits comparador_4bits_1 (
    .in_1(codificador_4bits_1_out_11), .in_2(codificador_4bits_2_out_11), .in_3(codificador_4bits_1_out_12),
    .in_4(codificador_4bits_2_out_12), .in_5(codificador_4bits_1_out_13), .in_6(codificador_4bits_2_out_13),
    .in_7(codificador_4bits_1_out_14), .in_8(codificador_4bits_2_out_14), .out_9(comparador_4bits_1_out_9));
  codificador_4bits codificador_4bits_3 (
    .in_1(in_1), .in_2(in_7), .in_3(in_13), .in_4(in_19), .in_5(in_25), .in_6(in_31), .in_7(in_37),
    .in_8(in_43), .in_9(in_49), .in_10(in_55), .out_11(codificador_4bits_3_out_11),
    .out_12(codificador_4bits_3_out_12), .out_13(codificador_4bits_3_out_13),
    .out_14(codificador_4bits_3_out_14));
  codificador_4bits codificador_4bits_4 (
    .in_1(in_61), .in_2(in_67), .in_3(in_73), .in_4(in_79), .in_5(in_85), .in_6(in_91), .in_7(in_97),
    .in_8(in_103), .in_9(in_109), .in_10(in_115), .out_11(codificador_4bits_4_out_11),
    .out_12(codificador_4bits_4_out_12), .out_13(codificador_4bits_4_out_13),
    .out_14(codificador_4bits_4_out_14));
  comparador_4bits comparador_4bits_2 (
    .in_1(codificador_4bits_3_out_11), .in_2(codificador_4bits_4_out_11), .in_3(codificador_4bits_3_out_12),
    .in_4(codificador_4bits_4_out_12), .in_5(codificador_4bits_3_out_13), .in_6(codificador_4bits_4_out_13),
    .in_7(codificador_4bits_3_out_14), .in_8(codificador_4bits_4_out_14), .out_9(comparador_4bits_2_out_9));
  codificador_4bits codificador_4bits_5 (
    .in_1(in_2), .in_2(in_8), .in_3(in_14), .in_4(in_20), .in_5(in_26), .in_6(in_32), .in_7(in_38),
    .in_8(in_44), .in_9(in_50), .in_10(in_56), .out_11(codificador_4bits_5_out_11),
    .out_12(codificador_4bits_5_out_12), .out_13(codificador_4bits_5_out_13),
    .out_14(codificador_4bits_5_out_14));
  codificador_4bits codificador_4bits_6 (
    .in_1(in_62), .in_2(in_68), .in_3(in_74), .in_4(in_80), .in_5(in_86), .in_6(in_92), .in_7(in_98),
    .in_8(in_104), .in_9(in_110), .in_10(in_116), .out_11(codificador_4bits_6_out_11),
    .out_12(codificador_4bits_6_out_12), .out_13(codificador_4bits_6_out_13),
    .out_14(codificador_4bits_6_out_14));
  comparador_4bits comparador_4bits_3 (
    .in_1(codificador_4bits_5_out_11), .in_2(codificador_4bits_6_out_11), .in_3(codificador_4bits_5_out_12),
    .in_4(codificador_4bits_6_out_12), .in_5(codificador_4bits_5_out_13), .in_6(codificador_4bits_6_out_13),
    .in_7(codificador_4bits_5_out_14), .in_8(codificador_4bits_6_out_14), .out_9(comparador_4bits_3_out_9));
  codificador_4bits codificador_4bits_7 (
    .in_1(in_6), .in_2(in_12), .in_3(in_18), .in_4(in_24), .in_5(in_30), .in_6(in_36), .in_7(in_42),
    .in_8(in_48), .in_9(in_54), .in_10(in_60), .out_11(codificador_4bits_7_out_11),
    .out_12(codificador_4bits_7_out_12), .out_13(codificador_4bits_7_out_13),
    .out_14(codificador_4bits_7_out_14));
  codificador_4bits codificador_4bits_8 (
    .in_1(in_66), .in_2(in_72), .in_3(in_78), .in_4(in_84), .in_5(in_90), .in_6(in_96), .in_7(in_102),
    .in_8(in_108), .in_9(in_114), .in_10(in_120), .out_11(codificador_4bits_8_out_11),
    .out_12(codificador_4bits_8_out_12), .out_13(codificador_4bits_8_out_13),
    .out_14(codificador_4bits_8_out_14));
  comparador_4bits comparador_4bits_4 (
    .in_1(codificador_4bits_7_out_11), .in_2(codificador_4bits_8_out_11), .in_3(codificador_4bits_7_out_12),
    .in_4(codificador_4bits_8_out_12), .in_5(codificador_4bits_7_out_13), .in_6(codificador_4bits_8_out_13),
    .in_7(codificador_4bits_7_out_14), .in_8(codificador_4bits_8_out_14), .out_9(comparador_4bits_4_out_9));
  codificador_4bits codificador_4bits_9 (
    .in_1(in_3), .in_2(in_9), .in_3(in_15), .in_4(in_21), .in_5(in_27), .in_6(in_33), .in_7(in_39),
    .in_8(in_45), .in_9(in_51), .in_10(in_57), .out_11(codificador_4bits_9_out_11),
    .out_12(codificador_4bits_9_out_12), .out_13(codificador_4bits_9_out_13),
    .out_14(codificador_4bits_9_out_14));
  codificador_4bits codificador_4bits_10 (
    .in_1(in_63), .in_2(in_69), .in_3(in_75), .in_4(in_81), .in_5(in_87), .in_6(in_93), .in_7(in_99),
    .in_8(in_105), .in_9(in_111), .in_10(in_117), .out_11(codificador_4bits_10_out_11),
    .out_12(codificador_4bits_10_out_12), .out_13(codificador_4bits_10_out_13),
    .out_14(codificador_4bits_10_out_14));
  comparador_4bits comparador_4bits_5 (
    .in_1(codificador_4bits_9_out_11), .in_2(codificador_4bits_10_out_11), .in_3(codificador_4bits_9_out_12),
    .in_4(codificador_4bits_10_out_12), .in_5(codificador_4bits_9_out_13),
    .in_6(codificador_4bits_10_out_13), .in_7(codificador_4bits_9_out_14),
    .in_8(codificador_4bits_10_out_14), .out_9(comparador_4bits_5_out_9));
  codificador_4bits codificador_4bits_11 (
    .in_1(in_4), .in_2(in_10), .in_3(in_16), .in_4(in_22), .in_5(in_28), .in_6(in_34), .in_7(in_40),
    .in_8(in_46), .in_9(in_52), .in_10(in_58), .out_11(codificador_4bits_11_out_11),
    .out_12(codificador_4bits_11_out_12), .out_13(codificador_4bits_11_out_13),
    .out_14(codificador_4bits_11_out_14));
  codificador_4bits codificador_4bits_12 (
    .in_1(in_64), .in_2(in_70), .in_3(in_76), .in_4(in_82), .in_5(in_88), .in_6(in_94), .in_7(in_100),
    .in_8(in_106), .in_9(in_112), .in_10(in_118), .out_11(codificador_4bits_12_out_11),
    .out_12(codificador_4bits_12_out_12), .out_13(codificador_4bits_12_out_13),
    .out_14(codificador_4bits_12_out_14));
  comparador_4bits comparador_4bits_6 (
    .in_1(codificador_4bits_11_out_11), .in_2(codificador_4bits_12_out_11),
    .in_3(codificador_4bits_11_out_12), .in_4(codificador_4bits_12_out_12),
    .in_5(codificador_4bits_11_out_13), .in_6(codificador_4bits_12_out_13),
    .in_7(codificador_4bits_11_out_14), .in_8(codificador_4bits_12_out_14), .out_9(comparador_4bits_6_out_9));
  and_nand and_nand_1 (.in_1(comparador_4bits_6_out_9), .in_2(comparador_4bits_5_out_9), .out_3(and_nand_1_out_3));
  and_nand and_nand_2 (.in_1(comparador_4bits_4_out_9), .in_2(comparador_4bits_3_out_9), .out_3(and_nand_2_out_3));
  and_nand and_nand_3 (.in_1(comparador_4bits_2_out_9), .in_2(comparador_4bits_1_out_9), .out_3(and_nand_3_out_3));
  and_nand and_nand_4 (.in_1(and_nand_1_out_3), .in_2(and_nand_2_out_3), .out_3(and_nand_4_out_3));
  and_nand and_nand_5 (.in_1(and_nand_4_out_3), .in_2(and_nand_3_out_3), .out_3(out_121));
endmodule

module codificador_4bits (
  input  in_1,
  input  in_2,
  input  in_3,
  input  in_4,
  input  in_5,
  input  in_6,
  input  in_7,
  input  in_8,
  input  in_9,
  input  in_10,
  output out_11,
  output out_12,
  output out_13,
  output out_14
);

  wire or_nand_2_out_3, or_nand_3_out_3, or_nand_4_out_3, or_nand_5_out_3, or_nand_8_out_3, or_nand_9_out_3,
       or_nand_10_out_3, or_nand_11_out_3;

  or_nand or_nand_1 (.in_1(in_2), .in_2(in_1), .out_3(out_11));
  or_nand or_nand_2 (.in_1(in_6), .in_2(in_5), .out_3(or_nand_2_out_3));
  or_nand or_nand_3 (.in_1(in_4), .in_2(in_3), .out_3(or_nand_3_out_3));
  or_nand or_nand_4 (.in_1(in_8), .in_2(in_7), .out_3(or_nand_4_out_3));
  or_nand or_nand_5 (.in_1(in_4), .in_2(in_3), .out_3(or_nand_5_out_3));
  or_nand or_nand_6 (.in_1(or_nand_2_out_3), .in_2(or_nand_3_out_3), .out_3(out_12));
  or_nand or_nand_7 (.in_1(or_nand_4_out_3), .in_2(or_nand_5_out_3), .out_3(out_13));
  or_nand or_nand_8 (.in_1(in_9), .in_2(in_7), .out_3(or_nand_8_out_3));
  or_nand or_nand_9 (.in_1(or_nand_8_out_3), .in_2(or_nand_10_out_3), .out_3(or_nand_9_out_3));
  or_nand or_nand_10 (.in_1(in_5), .in_2(in_3), .out_3(or_nand_10_out_3));
  or_nand or_nand_11 (.in_1(in_1), .in_2(in_1), .out_3(or_nand_11_out_3));
  or_nand or_nand_12 (.in_1(or_nand_9_out_3), .in_2(or_nand_11_out_3), .out_3(out_14));
endmodule

module or_nand (
  input  in_1,
  input  in_2,
  output out_3
);

  wire nand_1_out, nand_2_out;

  nand nand_1 (nand_1_out, in_1, in_1);
  nand nand_2 (nand_2_out, in_2, in_2);
  nand nand_3 (out_3, nand_1_out, nand_2_out);
endmodule
